// Logisim project 1-Addition&Subtraction Circuit.circ as structural Verilog: 5 circuits, main circuit Half Adder
// HA
module Half_Adder (
  input  A,
  input  B,
  output S,
  output C
);

  xor xor_1 (S, A, B);
  and and_1 (C, A, B);
endmodule

// FA
module Fall_Adder (
  input  A,
  input  B,
  input  C,
  output out_4,
  output out_5
);

  wire half_adder_1_c, half_adder_1_s, half_adder_2_c;

  Half_Adder half_adder_1 (.A(A), .B(B), .S(half_adder_1_s), .C(half_adder_1_c));
  Half_Adder half_adder_2 (.A(half_adder_1_s), .B(C), .S(out_4), .C(half_adder_2_c));
  or or_1 (out_5, half_adder_2_c, half_adder_1_c);
endmodule

module _2_s_Complement (
  input  A3,
  input  A2,
  input  A1,
  input  Ao,
  output R4,
  output R3,
  output R2,
  output R1
);

  wire or_1_out, or_2_out;

  xor xor_1 (R4, A3, or_1_out);
  or or_1 (or_1_out, A2, or_2_out);
  or or_2 (or_2_out, Ao, A1);
  xor xor_2 (R3, A2, or_2_out);
  xor xor_3 (R2, A1, Ao);

  assign R1 = Ao;
endmodule

// Check
module Check (
  input  A4,
  input  A3,
  input  A2,
  input  A1,
  input  Ao,
  output S4,
  output S3,
  output S2,
  output S1
);

  wire half_adder_2_c, half_adder_3_c, half_adder_4_c, n2_s_complement_1_r1, n2_s_complement_1_r2,
       n2_s_complement_1_r3, n2_s_complement_1_r4, not_1_out, xnor_1_out, xnor_2_out, xnor_3_out, xnor_4_out;

  not not_1 (not_1_out, A4);
  xnor xnor_1 (xnor_1_out, n2_s_complement_1_r4, A4);
  Half_Adder half_adder_1 (.A(half_adder_2_c), .B(xnor_1_out), .S(S4));  // open: C
  xnor xnor_2 (xnor_2_out, n2_s_complement_1_r3, A4);
  Half_Adder half_adder_2 (.A(half_adder_3_c), .B(xnor_2_out), .S(S3), .C(half_adder_2_c));
  _2_s_Complement u_2_s_complement_1 (
    .A3(A3), .A2(A2), .A1(A1), .Ao(Ao), .R4(n2_s_complement_1_r4), .R3(n2_s_complement_1_r3),
    .R2(n2_s_complement_1_r2), .R1(n2_s_complement_1_r1));
  xnor xnor_3 (xnor_3_out, n2_s_complement_1_r2, A4);
  Half_Adder half_adder_3 (.A(half_adder_4_c), .B(xnor_3_out), .S(S2), .C(half_adder_3_c));
  xnor xnor_4 (xnor_4_out, n2_s_complement_1_r1, A4);
  Half_Adder half_adder_4 (.A(not_1_out), .B(xnor_4_out), .S(S1), .C(half_adder_4_c));
endmodule

// Add/sub
module Addition_Sub (
  input  [4:0] b,
  input  [4:0] a,
  input  mode_sub,
  input  mode_add,
  output zero_flag,
  output sign,
  output [4:0] n
);

  wire and_1_out, and_2_out, and_3_out, and_4_out, check_1_s1, check_1_s2, check_1_s3, check_1_s4,
       check_3_s1, check_3_s2, check_3_s3, check_3_s4, fall_adder_1_out_4, fall_adder_1_out_5,
       fall_adder_2_out_4, fall_adder_2_out_5, fall_adder_3_out_4, fall_adder_3_out_5, fall_adder_4_out_4,
       fall_adder_4_out_5, fall_adder_5_out_4, fall_adder_5_out_5, not_1_out, or_1_out, or_3_out, xor_1_out;
  wire [4:0] multiplexer_1_out, multiplexer_2_out;

  and and_1 (and_1_out, multiplexer_2_out[4], fall_adder_1_out_4);
  or or_1 (or_1_out, and_1_out, and_2_out);
  xor xor_1 (xor_1_out, and_4_out, multiplexer_1_out[4]);
  and and_2 (and_2_out, fall_adder_1_out_4, xor_1_out);
  or or_2 (sign, or_1_out, and_3_out);
  and and_3 (and_3_out, multiplexer_2_out[4], xor_1_out);
  Fall_Adder fall_adder_1 (
    .A(fall_adder_2_out_5), .B(multiplexer_2_out[4]), .C(xor_1_out), .out_4(fall_adder_1_out_4),
    .out_5(fall_adder_1_out_5));
  Check check_1 (
    .A4(xor_1_out), .A3(multiplexer_1_out[3]), .A2(multiplexer_1_out[2]), .A1(multiplexer_1_out[1]),
    .Ao(multiplexer_1_out[0]), .S4(check_1_s4), .S3(check_1_s3), .S2(check_1_s2), .S1(check_1_s1));
  Fall_Adder fall_adder_2 (
    .A(fall_adder_3_out_5), .B(check_3_s4), .C(check_1_s4), .out_4(fall_adder_2_out_4),
    .out_5(fall_adder_2_out_5));
  Check check_2 (
    .A4(sign), .A3(fall_adder_2_out_4), .A2(fall_adder_3_out_4), .A1(fall_adder_4_out_4),
    .Ao(fall_adder_5_out_4), .S4(n[3]), .S3(n[2]), .S2(n[1]), .S1(n[0]));
  xor xor_2 (n[4], fall_adder_2_out_5, fall_adder_1_out_5);
  Multiplexer #(.width(5), .enable("false")) multiplexer_1 (
    .in0({5{1'b0}}), .in1(b), .out(multiplexer_1_out), .sel(or_3_out));
  Fall_Adder fall_adder_3 (
    .A(fall_adder_4_out_5), .B(check_3_s3), .C(check_1_s3), .out_4(fall_adder_3_out_4),
    .out_5(fall_adder_3_out_5));
  Check check_3 (
    .A4(multiplexer_2_out[4]), .A3(multiplexer_2_out[3]), .A2(multiplexer_2_out[2]),
    .A1(multiplexer_2_out[1]), .Ao(multiplexer_2_out[0]), .S4(check_3_s4), .S3(check_3_s3), .S2(check_3_s2),
    .S1(check_3_s1));
  Fall_Adder fall_adder_4 (
    .A(fall_adder_5_out_5), .B(check_3_s2), .C(check_1_s2), .out_4(fall_adder_4_out_4),
    .out_5(fall_adder_4_out_5));
  nor nor_1 (zero_flag, n[4], n[3], n[2], n[1], n[0]);
  Fall_Adder fall_adder_5 (
    .A(1'b0), .B(check_3_s1), .C(check_1_s1), .out_4(fall_adder_5_out_4), .out_5(fall_adder_5_out_5));
  Multiplexer #(.width(5), .enable("false")) multiplexer_2 (
    .in0({5{1'b0}}), .in1(a), .out(multiplexer_2_out), .sel(or_3_out));
  and and_4 (and_4_out, not_1_out, mode_sub);
  or or_3 (or_3_out, mode_sub, mode_add);
  not not_1 (not_1_out, mode_add);
endmodule
