// Logisim project 2-Multiplication Circuit.circ as structural Verilog: 4 circuits, main circuit Half Adder
// HA
module Half_Adder (
  input  A,
  input  B,
  output S,
  output C
);

  xor xor_1 (S, A, B);
  and and_1 (C, B, A);
endmodule

// FA
module Full_Adder (
  input  A,
  input  B,
  input  Ci,
  output S,
  output C
);

  wire half_adder_1_c, half_adder_1_s, half_adder_2_c;

  Half_Adder half_adder_1 (.A(A), .B(B), .S(half_adder_1_s), .C(half_adder_1_c));
  Half_Adder half_adder_2 (.A(half_adder_1_s), .B(Ci), .S(S), .C(half_adder_2_c));
  or or_1 (C, half_adder_1_c, half_adder_2_c);
endmodule

module _4_bits_adder (
  input  a0,
  input  a1,
  input  a2,
  input  a3,
  input  b0,
  input  b1,
  input  b2,
  input  b3,
  output S0,
  output S1,
  output S2,
  output S3,
  output Co
);

  wire full_adder_1_c, full_adder_2_c, full_adder_3_c;

  Full_Adder full_adder_1 (.A(a0), .B(b0), .Ci(1'b0), .S(S0), .C(full_adder_1_c));
  Full_Adder full_adder_2 (.A(a1), .B(b1), .Ci(full_adder_1_c), .S(S1), .C(full_adder_2_c));
  Full_Adder full_adder_3 (.A(a2), .B(b2), .Ci(full_adder_2_c), .S(S2), .C(full_adder_3_c));
  Full_Adder full_adder_4 (.A(a3), .B(b3), .Ci(full_adder_3_c), .S(S3), .C(Co));
endmodule

module Multiplier (
  input  [4:0] a,
  input  [4:0] b,
  input  mode,
  output [7:0] out_4,
  output sign_flag,
  output zero_flag
);

  wire a0b1_out, a0b2_out, a0b3_out, a1b0_out, a1b1_out, a1b2_out, a1b3_out, a2b0_out, a2b1_out, a2b2_out,
       a2b3_out, a3b0_out, a3b1_out, a3b2_out, a3b3_out, n4_bits_adder_1_co, n4_bits_adder_1_s1,
       n4_bits_adder_1_s2, n4_bits_adder_1_s3, n4_bits_adder_2_co, n4_bits_adder_2_s1, n4_bits_adder_2_s2,
       n4_bits_adder_2_s3, nor_1_out, xor_1_out;
  wire [4:0] multiplexer_1_out, multiplexer_2_out;

  and a1b3 (a1b3_out, multiplexer_1_out[1], multiplexer_2_out[3]);
  xor xor_1 (xor_1_out, multiplexer_1_out[4], multiplexer_2_out[4]);
  and a1b2 (a1b2_out, multiplexer_1_out[1], multiplexer_2_out[2]);
  and a1b1 (a1b1_out, multiplexer_1_out[1], multiplexer_2_out[1]);
  and a1b0 (a1b0_out, multiplexer_1_out[1], multiplexer_2_out[0]);
  _4_bits_adder u_4_bits_adder_1 (
    .a0(a0b1_out), .a1(a0b2_out), .a2(a0b3_out), .a3(1'b0), .b0(a1b0_out), .b1(a1b1_out), .b2(a1b2_out),
    .b3(a1b3_out), .S0(out_4[1]), .S1(n4_bits_adder_1_s1), .S2(n4_bits_adder_1_s2), .S3(n4_bits_adder_1_s3),
    .Co(n4_bits_adder_1_co));
  _4_bits_adder u_4_bits_adder_2 (
    .a0(a2b0_out), .a1(a2b1_out), .a2(a2b2_out), .a3(a2b3_out), .b0(n4_bits_adder_1_s1),
    .b1(n4_bits_adder_1_s2), .b2(n4_bits_adder_1_s3), .b3(n4_bits_adder_1_co), .S0(out_4[2]),
    .S1(n4_bits_adder_2_s1), .S2(n4_bits_adder_2_s2), .S3(n4_bits_adder_2_s3), .Co(n4_bits_adder_2_co));
  and a0b3 (a0b3_out, multiplexer_1_out[0], multiplexer_2_out[3]);
  and a0b2 (a0b2_out, multiplexer_1_out[0], multiplexer_2_out[2]);
  _4_bits_adder u_4_bits_adder_3 (
    .a0(a3b0_out), .a1(a3b1_out), .a2(a3b2_out), .a3(a3b3_out), .b0(n4_bits_adder_2_s1),
    .b1(n4_bits_adder_2_s2), .b2(n4_bits_adder_2_s3), .b3(n4_bits_adder_2_co), .S0(out_4[3]), .S1(out_4[4]),
    .S2(out_4[5]), .S3(out_4[6]), .Co(out_4[7]));
  and and_1 (sign_flag, xor_1_out, mode);
  and a0b1 (a0b1_out, multiplexer_1_out[0], multiplexer_2_out[1]);
  and a0b0 (out_4[0], multiplexer_1_out[0], multiplexer_2_out[0]);
  nor nor_1 (nor_1_out, out_4[0], out_4[1], out_4[2], out_4[3], out_4[4], out_4[5], out_4[6], out_4[7]);
  and and_2 (zero_flag, nor_1_out, mode);
  and a2b2 (a2b2_out, multiplexer_1_out[2], multiplexer_2_out[2]);
  and a2b3 (a2b3_out, multiplexer_1_out[2], multiplexer_2_out[3]);
  and a2b0 (a2b0_out, multiplexer_1_out[2], multiplexer_2_out[0]);
  and a2b1 (a2b1_out, multiplexer_1_out[2], multiplexer_2_out[1]);
  and a3b3 (a3b3_out, multiplexer_1_out[3], multiplexer_2_out[3]);
  and a3b2 (a3b2_out, multiplexer_1_out[3], multiplexer_2_out[2]);
  and a3b1 (a3b1_out, multiplexer_1_out[3], multiplexer_2_out[1]);
  and a3b0 (a3b0_out, multiplexer_1_out[3], multiplexer_2_out[0]);
  Multiplexer #(.width(5), .enable("false")) multiplexer_1 (
    .in0({5{1'b0}}), .in1(a), .out(multiplexer_1_out), .sel(mode));
  Multiplexer #(.width(5), .enable("false")) multiplexer_2 (
    .in0({5{1'b0}}), .in1(b), .out(multiplexer_2_out), .sel(mode));
endmodule
