// Logisim project 3-Division Circuit.circ as structural Verilog: 6 circuits, main circuit Half Adder
// HA
module Half_Adder (
  input  A,
  input  B,
  output S,
  output C
);

  xor xor_1 (S, A, B);
  and and_1 (C, A, B);
endmodule

// FA
module Full_Adder (
  input  A,
  input  B,
  input  C,
  output out_4,
  output out_5
);

  wire half_adder_1_c, half_adder_1_s, half_adder_2_c;

  Half_Adder half_adder_1 (.A(A), .B(B), .S(half_adder_1_s), .C(half_adder_1_c));
  Half_Adder half_adder_2 (.A(half_adder_1_s), .B(C), .S(out_4), .C(half_adder_2_c));
  or or_1 (out_5, half_adder_2_c, half_adder_1_c);
endmodule

module Subtractor (
  input  A3,
  input  A2,
  input  A1,
  input  Ao,
  input  B3,
  input  B2,
  input  B1,
  input  Bo,
  output out_9,
  output out_10,
  output out_11,
  output out_12,
  output out_13
);

  wire full_adder_2_out_5, full_adder_3_out_5, full_adder_4_out_5, xor_1_out, xor_2_out, xor_3_out, xor_4_out;

  xor xor_1 (xor_1_out, B3, 1'b1);
  Full_Adder full_adder_1 (.A(A3), .B(xor_1_out), .C(full_adder_2_out_5), .out_4(out_10), .out_5(out_9));
  xor xor_2 (xor_2_out, B2, 1'b1);
  Full_Adder full_adder_2 (.A(A2), .B(xor_2_out), .C(full_adder_3_out_5), .out_4(out_13), .out_5(full_adder_2_out_5));
  xor xor_3 (xor_3_out, B1, 1'b1);
  Full_Adder full_adder_3 (.A(A1), .B(xor_3_out), .C(full_adder_4_out_5), .out_4(out_11), .out_5(full_adder_3_out_5));
  xor xor_4 (xor_4_out, Bo, 1'b1);
  Full_Adder full_adder_4 (.A(Ao), .B(xor_4_out), .C(1'b1), .out_4(out_12), .out_5(full_adder_4_out_5));
endmodule

module Division_Multiplixer (
  input  in_1,
  input  in_2,
  input  in_3,
  input  in_4,
  input  in_5,
  input  in_6,
  input  in_7,
  input  in_8,
  input  in_9,
  output out_10,
  output out_11,
  output out_12,
  output out_13
);

  Multiplexer #(.enable("false")) multiplexer_1 (.in0(in_1), .in1(in_5), .out(out_10), .sel(in_9));
  Multiplexer #(.enable("false")) multiplexer_2 (.in0(in_2), .in1(in_6), .out(out_11), .sel(in_9));
  Multiplexer #(.enable("false")) multiplexer_3 (.in0(in_3), .in1(in_7), .out(out_12), .sel(in_9));
  Multiplexer #(.enable("false")) multiplexer_4 (.in0(in_4), .in1(in_8), .out(out_13), .sel(in_9));
endmodule

module _4_Bits_Division (
  input  A3,
  input  A2,
  input  A1,
  input  A0,
  input  B3,
  input  B2,
  input  B1,
  input  B0,
  output out_9,
  output out_10,
  output Q1,
  output Q0
);

  wire division_multiplixer_1_out_11, division_multiplixer_1_out_12, division_multiplixer_1_out_13,
       division_multiplixer_2_out_11, division_multiplixer_2_out_12, division_multiplixer_2_out_13,
       division_multiplixer_3_out_11, division_multiplixer_3_out_12, division_multiplixer_3_out_13,
       subtractor_1_out_10, subtractor_1_out_11, subtractor_1_out_12, subtractor_1_out_13,
       subtractor_2_out_10, subtractor_2_out_11, subtractor_2_out_12, subtractor_2_out_13,
       subtractor_3_out_10, subtractor_3_out_11, subtractor_3_out_12, subtractor_3_out_13;

  Subtractor subtractor_1 (
    .out_9(out_9), .A3(1'b0), .A2(1'b0), .A1(1'b0), .Ao(A3), .B3(B3), .B2(B2), .B1(B1), .Bo(B0),
    .out_10(subtractor_1_out_10), .out_13(subtractor_1_out_13), .out_11(subtractor_1_out_11),
    .out_12(subtractor_1_out_12));
  Division_Multiplixer division_multiplixer_1 (
    .in_9(out_9), .in_1(1'b0), .in_2(1'b0), .in_3(1'b0), .in_4(A3), .in_5(subtractor_1_out_10),
    .in_6(subtractor_1_out_13), .in_7(subtractor_1_out_11), .in_8(subtractor_1_out_12),
    .out_11(division_multiplixer_1_out_11), .out_12(division_multiplixer_1_out_12),
    .out_13(division_multiplixer_1_out_13));  // open: out_10
  Division_Multiplixer division_multiplixer_2 (
    .in_9(out_10), .in_1(division_multiplixer_1_out_11), .in_2(division_multiplixer_1_out_12),
    .in_3(division_multiplixer_1_out_13), .in_4(A2), .in_5(subtractor_2_out_10), .in_6(subtractor_2_out_13),
    .in_7(subtractor_2_out_11), .in_8(subtractor_2_out_12), .out_11(division_multiplixer_2_out_11),
    .out_12(division_multiplixer_2_out_12), .out_13(division_multiplixer_2_out_13));  // open: out_10
  Subtractor subtractor_2 (
    .out_9(out_10), .A3(division_multiplixer_1_out_11), .A2(division_multiplixer_1_out_12),
    .A1(division_multiplixer_1_out_13), .Ao(A2), .B3(B3), .B2(B2), .B1(B1), .Bo(B0),
    .out_10(subtractor_2_out_10), .out_13(subtractor_2_out_13), .out_11(subtractor_2_out_11),
    .out_12(subtractor_2_out_12));
  Subtractor subtractor_3 (
    .out_9(Q1), .A3(division_multiplixer_2_out_11), .A2(division_multiplixer_2_out_12),
    .A1(division_multiplixer_2_out_13), .Ao(A1), .B3(B3), .B2(B2), .B1(B1), .Bo(B0),
    .out_10(subtractor_3_out_10), .out_13(subtractor_3_out_13), .out_11(subtractor_3_out_11),
    .out_12(subtractor_3_out_12));
  Division_Multiplixer division_multiplixer_3 (
    .in_9(Q1), .in_1(division_multiplixer_2_out_11), .in_2(division_multiplixer_2_out_12),
    .in_3(division_multiplixer_2_out_13), .in_4(A1), .in_5(subtractor_3_out_10), .in_6(subtractor_3_out_13),
    .in_7(subtractor_3_out_11), .in_8(subtractor_3_out_12), .out_11(division_multiplixer_3_out_11),
    .out_12(division_multiplixer_3_out_12), .out_13(division_multiplixer_3_out_13));  // open: out_10
  Subtractor subtractor_4 (
    .out_9(Q0), .A3(division_multiplixer_3_out_11), .A2(division_multiplixer_3_out_12),
    .A1(division_multiplixer_3_out_13), .Ao(A0), .B3(B3), .B2(B2), .B1(B1), .Bo(B0));  // open: out_10, out_13, out_11, out_12

  // Notes on the sheet:
  //   Q3
  //   Q2
endmodule

module Full_Division (
  input  [4:0] a,
  input  [4:0] b,
  input  mode,
  output Div__by_zero_Flag,
  output [3:0] q,
  output sign,
  output zero_flag
);

  wire nor_1_out, nor_2_out, xor_1_out;
  wire [3:0] n4_bits_division_1_q0;
  wire [4:0] multiplexer_1_out, multiplexer_3_out;

  nor nor_1 (nor_1_out, multiplexer_1_out[3], multiplexer_1_out[2], multiplexer_1_out[1], multiplexer_1_out[0]);
  and and_1 (zero_flag, nor_1_out, mode);
  xor xor_1 (xor_1_out, multiplexer_1_out[4], multiplexer_3_out[4]);
  Multiplexer #(.width(5), .enable("false")) multiplexer_1 (
    .in0({5{1'b0}}), .in1(a), .out(multiplexer_1_out), .sel(mode));
  _4_Bits_Division u_4_bits_division_1 (
    .A3(multiplexer_1_out[3]), .A2(multiplexer_1_out[2]), .A1(multiplexer_1_out[1]),
    .A0(multiplexer_1_out[0]), .B3(multiplexer_3_out[3]), .B2(multiplexer_3_out[2]),
    .B1(multiplexer_3_out[1]), .B0(multiplexer_3_out[0]), .out_9(n4_bits_division_1_q0[3]),
    .out_10(n4_bits_division_1_q0[2]), .Q1(n4_bits_division_1_q0[1]), .Q0(n4_bits_division_1_q0[0]));
  and and_2 (sign, xor_1_out, mode);
  Multiplexer #(.width(4), .enable("false")) multiplexer_2 (
    .in0(4'b0000), .in1(n4_bits_division_1_q0), .out(q), .sel(mode));
  Multiplexer #(.width(5), .enable("false")) multiplexer_3 (
    .in0({5{1'b0}}), .in1(b), .out(multiplexer_3_out), .sel(mode));
  and and_3 (Div__by_zero_Flag, mode, nor_2_out);
  nor nor_2 (nor_2_out, multiplexer_3_out[0], multiplexer_3_out[1], multiplexer_3_out[2], multiplexer_3_out[3]);
endmodule
