// Logisim project 4-Binary To BCD Circuit.circ as structural Verilog: 2 circuits, main circuit BinaryToBCD
module add_shift_3 (
  input  D,
  input  C,
  input  B,
  input  A,
  output W,
  output Z,
  output Y,
  output X
);

  wire not_1_out, not_2_out, not_3_out, not_4_out, w_2_out, w_3_out, w_out, x_2_out, x_3_out, x_out, y_2_out,
       y_out, z_2_out, z_3_out, z_out;

  not not_1 (not_1_out, D);
  not not_2 (not_2_out, C);
  not not_3 (not_3_out, B);
  not not_4 (not_4_out, A);
  and u_x (x_out, not_4_out, B, D);
  and x_2 (x_2_out, not_4_out, B, C);
  or or_1 (X, x_out, x_2_out, x_3_out);
  and x_3 (x_3_out, A, not_2_out, not_3_out);
  and u_w (w_out, A, not_2_out, not_3_out, not_1_out);
  and w_2 (w_2_out, not_4_out, B, C, not_1_out);
  and w_3 (w_3_out, not_4_out, not_3_out, D);
  or or_2 (W, w_out, w_2_out, w_3_out);
  and u_z (z_out, not_4_out, C, D);
  and z_2 (z_2_out, not_4_out, not_3_out, C);
  or or_3 (Z, z_out, z_2_out, z_3_out);
  and z_3 (z_3_out, A, not_3_out, not_2_out, not_1_out);
  and u_y (y_out, A, not_3_out, not_2_out, D);
  and y_2 (y_2_out, not_4_out, B, not_2_out, not_1_out);
  or or_4 (Y, y_2_out, y_out);
endmodule

module BinaryToBCD (
  input  [7:0] _8_Bits_input,
  output [11:0] _12_Bits_Output
);

  wire add_shift_3_1_w, add_shift_3_1_x, add_shift_3_1_y, add_shift_3_1_z, add_shift_3_2_w, add_shift_3_2_x,
       add_shift_3_2_y, add_shift_3_2_z, add_shift_3_3_w, add_shift_3_3_x, add_shift_3_3_y, add_shift_3_3_z,
       add_shift_3_4_w, add_shift_3_4_x, add_shift_3_4_y, add_shift_3_4_z, add_shift_3_5_w, add_shift_3_5_y,
       add_shift_3_5_z;

  add_shift_3 add_shift_3_1 (
    .D(_8_Bits_input[5]), .C(_8_Bits_input[6]), .B(_8_Bits_input[7]), .A(1'b0), .W(add_shift_3_1_w),
    .Z(add_shift_3_1_z), .Y(add_shift_3_1_y), .X(add_shift_3_1_x));
  add_shift_3 add_shift_3_2 (
    .D(_8_Bits_input[4]), .C(add_shift_3_1_w), .B(add_shift_3_1_z), .A(add_shift_3_1_y), .W(add_shift_3_2_w),
    .Z(add_shift_3_2_z), .Y(add_shift_3_2_y), .X(add_shift_3_2_x));
  add_shift_3 add_shift_3_3 (
    .D(_8_Bits_input[3]), .C(add_shift_3_2_w), .B(add_shift_3_2_z), .A(add_shift_3_2_y), .W(add_shift_3_3_w),
    .Z(add_shift_3_3_z), .Y(add_shift_3_3_y), .X(add_shift_3_3_x));
  add_shift_3 add_shift_3_4 (
    .D(_8_Bits_input[2]), .C(add_shift_3_3_w), .B(add_shift_3_3_z), .A(add_shift_3_3_y), .W(add_shift_3_4_w),
    .Z(add_shift_3_4_z), .Y(add_shift_3_4_y), .X(add_shift_3_4_x));
  add_shift_3 add_shift_3_5 (
    .D(add_shift_3_3_x), .C(add_shift_3_2_x), .B(add_shift_3_1_x), .A(1'b0), .W(add_shift_3_5_w),
    .Z(add_shift_3_5_z), .Y(add_shift_3_5_y), .X(_12_Bits_Output[9]));
  add_shift_3 add_shift_3_6 (
    .D(add_shift_3_4_x), .C(add_shift_3_5_w), .B(add_shift_3_5_z), .A(add_shift_3_5_y),
    .W(_12_Bits_Output[5]), .Z(_12_Bits_Output[6]), .Y(_12_Bits_Output[7]), .X(_12_Bits_Output[8]));
  add_shift_3 add_shift_3_7 (
    .D(_8_Bits_input[1]), .C(add_shift_3_4_w), .B(add_shift_3_4_z), .A(add_shift_3_4_y),
    .W(_12_Bits_Output[1]), .Z(_12_Bits_Output[2]), .Y(_12_Bits_Output[3]), .X(_12_Bits_Output[4]));

  assign {_12_Bits_Output[11:10], _12_Bits_Output[0]} = {2'b00, _8_Bits_input[0]};
endmodule
