// Logisim project 5-BCD to 7-Segment Circuit.circ as structural Verilog: 1 circuit, main circuit BCD to 7-Segment
// BCD to 7
module BCD_to_7_Segment (
  input  A,
  input  B,
  input  C,
  input  D,
  input  Div__by_zero_Flag,
  output a_2,
  output b_2,
  output c_2,
  output d_2,
  output e,
  output f,
  output g
);

  wire a_out, b_out, B_prime_C_out, B_prime_D_prime_out, BC_prime_D_out, BC_prime_out, BD_out, BD_prime_out,
       c_out, C_prime_D_prime_out, CD_out, CD_prime_out, d_out, e_out, f_out, g_out, not_1_out, not_2_out,
       not_3_out, not_4_out;

  not not_1 (not_1_out, B);
  not not_2 (not_2_out, C);
  not not_3 (not_3_out, D);
  and BD (BD_out, B, D);
  and B_prime_D_prime (B_prime_D_prime_out, not_1_out, not_3_out);
  and CD (CD_out, C, D);
  and C_prime_D_prime (C_prime_D_prime_out, not_2_out, not_3_out);
  and CD_prime (CD_prime_out, C, not_3_out);
  and B_prime_C (B_prime_C_out, not_1_out, C);
  and BC_prime (BC_prime_out, B, not_2_out);
  and BD_prime (BD_prime_out, B, not_3_out);
  and BC_prime_D (BC_prime_D_out, D, BC_prime_out);
  not not_4 (not_4_out, Div__by_zero_Flag);
  or u_a (a_out, BD_out, B_prime_D_prime_out, A, C);
  or u_b (b_out, CD_out, not_1_out, C_prime_D_prime_out);
  or u_c (c_out, B, not_2_out, D);
  or u_d (d_out, A, B_prime_D_prime_out, CD_prime_out, B_prime_C_out, BC_prime_D_out);
  or u_e (e_out, B_prime_D_prime_out, CD_prime_out);
  or u_f (f_out, C_prime_D_prime_out, BC_prime_out, BD_prime_out, A);
  or u_g (g_out, CD_prime_out, B_prime_C_out, BC_prime_out, A);
  and and_1 (a_2, not_4_out, a_out);
  and and_2 (b_2, not_4_out, b_out);
  and and_3 (c_2, not_4_out, c_out);
  and and_4 (d_2, not_4_out, d_out);
  and and_5 (e, not_4_out, e_out);
  and and_6 (f, not_4_out, f_out);
  and and_7 (g, not_4_out, g_out);

  // Notes on the sheet:
  //   A
  //   B
  //   C
  //   D
endmodule
