// Logisim project 6-FullCircuit.circ as structural Verilog: 2 circuits, main circuit FinalCircuit
module FinalCircuit (
  input  [4:0] a,
  input  [4:0] b,
  input  [1:0] mode
);

  wire bcd_to_7_segment_1_a_2, bcd_to_7_segment_1_b_2, bcd_to_7_segment_1_c_2, bcd_to_7_segment_1_d_2,
       bcd_to_7_segment_1_e, bcd_to_7_segment_1_f, bcd_to_7_segment_1_g, bcd_to_7_segment_2_a_2,
       bcd_to_7_segment_2_b_2, bcd_to_7_segment_2_c_2, bcd_to_7_segment_2_d_2, bcd_to_7_segment_2_e,
       bcd_to_7_segment_2_f, bcd_to_7_segment_2_g, bcd_to_7_segment_3_a_2, bcd_to_7_segment_3_b_2,
       bcd_to_7_segment_3_c_2, bcd_to_7_segment_3_d_2, bcd_to_7_segment_3_e, bcd_to_7_segment_3_f,
       bcd_to_7_segment_3_g;
  wire [2:0] ALU_sign_zero_div;
  wire [7:0] ALU_result;
  wire [11:0] BCD__12_bits_output;

  ALU ALU (.a(a), .b(b), .mode(mode), .result(ALU_result), .sign_zero_div(ALU_sign_zero_div));
  BinaryToBCD BCD (._12_Bits_Output(BCD__12_bits_output), ._8_Bits_input(ALU_result));
  LED zero_flag (.in(ALU_sign_zero_div[1]));
  BCD_to_7_Segment bcd_to_7_segment_1 (
    .A(BCD__12_bits_output[11]), .B(BCD__12_bits_output[10]), .C(BCD__12_bits_output[9]),
    .D(BCD__12_bits_output[8]), .Div__by_zero_Flag(ALU_sign_zero_div[0]), .a_2(bcd_to_7_segment_1_a_2),
    .b_2(bcd_to_7_segment_1_b_2), .c_2(bcd_to_7_segment_1_c_2), .d_2(bcd_to_7_segment_1_d_2),
    .e(bcd_to_7_segment_1_e), .f(bcd_to_7_segment_1_f), .g(bcd_to_7_segment_1_g));
  LED div_by_zero (.in(ALU_sign_zero_div[0]));
  _7_Segment_Display u_7_segment_display_1 (
    .g(bcd_to_7_segment_1_g), .f(bcd_to_7_segment_1_f), .a(bcd_to_7_segment_1_a_2),
    .b(bcd_to_7_segment_1_b_2), .e(bcd_to_7_segment_1_e), .d(bcd_to_7_segment_1_d_2),
    .c(bcd_to_7_segment_1_c_2));  // open: dp
  LED negative (.in(ALU_sign_zero_div[2]));
  BCD_to_7_Segment bcd_to_7_segment_2 (
    .A(BCD__12_bits_output[7]), .B(BCD__12_bits_output[6]), .C(BCD__12_bits_output[5]),
    .D(BCD__12_bits_output[4]), .Div__by_zero_Flag(ALU_sign_zero_div[0]), .a_2(bcd_to_7_segment_2_a_2),
    .b_2(bcd_to_7_segment_2_b_2), .c_2(bcd_to_7_segment_2_c_2), .d_2(bcd_to_7_segment_2_d_2),
    .e(bcd_to_7_segment_2_e), .f(bcd_to_7_segment_2_f), .g(bcd_to_7_segment_2_g));
  _7_Segment_Display u_7_segment_display_2 (
    .g(bcd_to_7_segment_2_g), .f(bcd_to_7_segment_2_f), .a(bcd_to_7_segment_2_a_2),
    .b(bcd_to_7_segment_2_b_2), .e(bcd_to_7_segment_2_e), .d(bcd_to_7_segment_2_d_2),
    .c(bcd_to_7_segment_2_c_2));  // open: dp
  BCD_to_7_Segment bcd_to_7_segment_3 (
    .A(BCD__12_bits_output[3]), .B(BCD__12_bits_output[2]), .C(BCD__12_bits_output[1]),
    .D(BCD__12_bits_output[0]), .Div__by_zero_Flag(ALU_sign_zero_div[0]), .a_2(bcd_to_7_segment_3_a_2),
    .b_2(bcd_to_7_segment_3_b_2), .c_2(bcd_to_7_segment_3_c_2), .d_2(bcd_to_7_segment_3_d_2),
    .e(bcd_to_7_segment_3_e), .f(bcd_to_7_segment_3_f), .g(bcd_to_7_segment_3_g));
  _7_Segment_Display u_7_segment_display_3 (
    .g(bcd_to_7_segment_3_g), .f(bcd_to_7_segment_3_f), .a(bcd_to_7_segment_3_a_2),
    .b(bcd_to_7_segment_3_b_2), .e(bcd_to_7_segment_3_e), .d(bcd_to_7_segment_3_d_2),
    .c(bcd_to_7_segment_3_c_2));  // open: dp

  // Notes on the sheet:
  //   00 - ADD
  //   01 - SUBTRACT
  //   10 - MULTIPLY
  //   11 - DIVIDE
endmodule

module ALU (
  input  [4:0] a,
  input  [4:0] b,
  input  [1:0] mode,
  output [7:0] result,
  output [2:0] sign_zero_div
);

  wire Add_sub_sign, Add_sub_zero_flag, and_2_out, decoder_1_out0, decoder_1_out1, decoder_1_out2,
       decoder_1_out3, Divison_div__by_zero_flag, Divison_sign, Divison_zero_flag, Multiplication_sign_flag,
       Multiplication_zero_flag, not_1_out, not_2_out, not_3_out, or_1_out, or_3_out, or_4_out, or_5_out,
       or_7_out, or_9_out, or_11_out;
  wire [3:0] Divison_q;
  wire [4:0] Add_sub_n, Multiplication_out_4;

  Decoder #(.select(2), .enable("false")) decoder_1 (
    .out0(decoder_1_out0), .out1(decoder_1_out1), .out2(decoder_1_out2), .out3(decoder_1_out3), .sel(mode));
  Multiplier Multiplication (
    .a(a), .b(b), .mode(decoder_1_out2), .out_4({result[7:5], Multiplication_out_4}),
    .zero_flag(Multiplication_zero_flag), .sign_flag(Multiplication_sign_flag));
  Full_Division Divison (
    .mode(decoder_1_out3), .a(a), .b(b), .zero_flag(Divison_zero_flag), .sign(Divison_sign), .q(Divison_q),
    .Div__by_zero_Flag(Divison_div__by_zero_flag));
  Addition_Sub Add_sub (
    .mode_add(decoder_1_out0), .zero_flag(Add_sub_zero_flag), .b(b), .a(a), .sign(Add_sub_sign),
    .n(Add_sub_n), .mode_sub(decoder_1_out1));
  or or_1 (or_1_out, Add_sub_zero_flag, Divison_zero_flag);
  or or_2 (sign_zero_div[1], or_1_out, Multiplication_zero_flag);
  or or_3 (or_3_out, Add_sub_sign, Divison_sign);
  or or_4 (or_4_out, or_3_out, Multiplication_sign_flag);
  not not_1 (not_1_out, sign_zero_div[1]);
  not not_2 (not_2_out, sign_zero_div[1]);
  and and_1 (sign_zero_div[0], Divison_div__by_zero_flag, not_1_out);
  and and_2 (and_2_out, not_2_out, or_4_out);
  or or_5 (or_5_out, Multiplication_out_4[0], Divison_q[0]);
  or or_6 (result[0], or_5_out, Add_sub_n[0]);
  or or_7 (or_7_out, Multiplication_out_4[1], Divison_q[1]);
  or or_8 (result[1], or_7_out, Add_sub_n[1]);
  or or_9 (or_9_out, Multiplication_out_4[2], Divison_q[2]);
  or or_10 (result[2], or_9_out, Add_sub_n[2]);
  or or_11 (or_11_out, Divison_q[3], Multiplication_out_4[3]);
  or or_12 (result[3], or_11_out, Add_sub_n[3]);
  or or_13 (result[4], Multiplication_out_4[4], Add_sub_n[4]);
  not not_3 (not_3_out, sign_zero_div[0]);
  and and_3 (sign_zero_div[2], not_3_out, and_2_out);

  // Notes on the sheet:
  //   00 - ADD
  //   11 - DIVIDE
  //   01 - SUBTRACT
  //   10 - MULTIPLY
endmodule
