// Logisim project Projeeectt.circ as structural Verilog: 9 circuits, main circuit Full Adder
module main (
  input  A,
  input  B,
  output S,
  output C
);

  xor xor_1 (S, A, B);
  and and_1 (C, A, B);
endmodule

module Half_Adder (
  input  A,
  input  B,
  output S,
  output C
);

  xor xor_1 (S, A, B);
  and and_1 (C, A, B);
endmodule

module Full_Adder (
  input  A,
  input  B,
  input  C,
  output out_4,
  output out_5
);

  wire half_adder_1_c, half_adder_1_s, half_adder_2_c;

  Half_Adder half_adder_1 (.A(A), .B(B), .S(half_adder_1_s), .C(half_adder_1_c));
  Half_Adder half_adder_2 (.A(half_adder_1_s), .B(C), .S(out_4), .C(half_adder_2_c));
  or or_1 (out_5, half_adder_2_c, half_adder_1_c);
endmodule

module _2_s_Complement (
  input  S3,
  input  S2,
  input  S1,
  input  S0,
  output O0,
  output o2,
  output _01,
  output o3
);

  wire or_1_out, or_2_out;

  or or_1 (or_1_out, or_2_out, S2);
  xor xor_1 (o3, S3, or_1_out);
  or or_2 (or_2_out, S0, S1);
  xor xor_2 (o2, S2, or_2_out);
  xor xor_3 (_01, S1, S0);

  assign O0 = S0;
endmodule

module Check_2_s (
  input  Sign,
  input  A3,
  input  A2,
  input  A1,
  input  A0,
  output out_6,
  output out_7,
  output out_8,
  output out_9
);

  wire half_adder_2_c, half_adder_3_c, half_adder_4_c, n2_s_complement_1__01, n2_s_complement_1_o0,
       n2_s_complement_1_o2, n2_s_complement_1_o3, not_1_out, xnor_1_out, xnor_2_out, xnor_3_out, xnor_4_out;

  not not_1 (not_1_out, Sign);
  xnor xnor_1 (xnor_1_out, Sign, n2_s_complement_1_o3);
  Half_Adder half_adder_1 (.A(half_adder_2_c), .B(xnor_1_out), .S(out_6));  // open: C
  xnor xnor_2 (xnor_2_out, Sign, n2_s_complement_1_o2);
  _2_s_Complement u_2_s_complement_1 (
    .S3(A3), .S2(A2), .S1(A1), .S0(A0), .o3(n2_s_complement_1_o3), .o2(n2_s_complement_1_o2),
    ._01(n2_s_complement_1__01), .O0(n2_s_complement_1_o0));
  Half_Adder half_adder_2 (.A(half_adder_3_c), .B(xnor_2_out), .S(out_7), .C(half_adder_2_c));
  xnor xnor_3 (xnor_3_out, Sign, n2_s_complement_1__01);
  Half_Adder half_adder_3 (.A(half_adder_4_c), .B(xnor_3_out), .S(out_8), .C(half_adder_3_c));
  xnor xnor_4 (xnor_4_out, Sign, n2_s_complement_1_o0);
  Half_Adder half_adder_4 (.A(not_1_out), .B(xnor_4_out), .S(out_9), .C(half_adder_4_c));
endmodule

module Adder_sub (
  input  B4,
  input  A4,
  input  B3,
  input  A3,
  input  B2,
  input  A2,
  input  B1,
  input  A1,
  input  Bo,
  input  Ao,
  input  in_11,
  input  in_12,
  output R2,
  output R1,
  output out_15,
  output R4,
  output R3
);

  wire check_2_s_1_out_6, check_2_s_1_out_7, check_2_s_1_out_8, check_2_s_1_out_9, check_2_s_3_out_6,
       check_2_s_3_out_7, check_2_s_3_out_8, check_2_s_3_out_9, full_adder_1_out_4, full_adder_1_out_5,
       full_adder_2_out_4, full_adder_2_out_5, full_adder_3_out_4, full_adder_3_out_5, full_adder_4_out_4,
       full_adder_4_out_5, full_adder_5_out_4, full_adder_5_out_5, or_1_out, xor_1_out;

  xor xor_1 (xor_1_out, or_1_out, B4);
  xor xor_2 (out_15, full_adder_2_out_5, full_adder_1_out_5);
  Check_2_s check_2_s_1 (
    .Sign(xor_1_out), .A3(B3), .A2(B2), .A1(B1), .A0(Bo), .out_6(check_2_s_1_out_6),
    .out_7(check_2_s_1_out_7), .out_8(check_2_s_1_out_8), .out_9(check_2_s_1_out_9));
  Full_Adder full_adder_1 (
    .A(full_adder_2_out_5), .B(A4), .C(xor_1_out), .out_4(full_adder_1_out_4), .out_5(full_adder_1_out_5));
  Full_Adder full_adder_2 (
    .A(full_adder_3_out_5), .B(check_2_s_3_out_6), .C(check_2_s_1_out_6), .out_4(full_adder_2_out_4),
    .out_5(full_adder_2_out_5));
  Full_Adder full_adder_3 (
    .A(full_adder_4_out_5), .B(check_2_s_3_out_7), .C(check_2_s_1_out_7), .out_4(full_adder_3_out_4),
    .out_5(full_adder_3_out_5));
  Check_2_s check_2_s_2 (
    .Sign(full_adder_1_out_4), .A3(full_adder_2_out_4), .A2(full_adder_3_out_4), .A1(full_adder_4_out_4),
    .A0(full_adder_5_out_4), .out_6(R4), .out_7(R3), .out_8(R2), .out_9(R1));
  Full_Adder full_adder_4 (
    .A(full_adder_5_out_5), .B(check_2_s_3_out_8), .C(check_2_s_1_out_8), .out_4(full_adder_4_out_4),
    .out_5(full_adder_4_out_5));
  Check_2_s check_2_s_3 (
    .Sign(A4), .A3(A3), .A2(A2), .A1(A1), .A0(Ao), .out_6(check_2_s_3_out_6), .out_7(check_2_s_3_out_7),
    .out_8(check_2_s_3_out_8), .out_9(check_2_s_3_out_9));
  Full_Adder full_adder_5 (
    .A(1'b0), .B(check_2_s_3_out_9), .C(check_2_s_1_out_9), .out_4(full_adder_5_out_4),
    .out_5(full_adder_5_out_5));
  or or_1 (or_1_out, in_11, in_12);
endmodule

module _2_s (
  input  A3,
  input  A2,
  input  A1,
  input  Ao,
  output R4,
  output R3,
  output R2,
  output R1
);

  wire or_1_out, or_2_out;

  xor xor_1 (R4, A3, or_1_out);
  or or_1 (or_1_out, A2, or_2_out);
  or or_2 (or_2_out, Ao, A1);
  xor xor_2 (R3, A2, or_2_out);
  xor xor_3 (R2, A1, Ao);

  assign R1 = Ao;
endmodule

module check (
  input  A4,
  input  A3,
  input  A2,
  input  A1,
  input  Ao,
  output S4,
  output S3,
  output S2,
  output S1
);

  wire half_adder_2_c, half_adder_3_c, half_adder_4_c, n2_s_1_r1, n2_s_1_r2, n2_s_1_r3, n2_s_1_r4, not_1_out,
       xnor_1_out, xnor_2_out, xnor_3_out, xnor_4_out;

  not not_1 (not_1_out, A4);
  xnor xnor_1 (xnor_1_out, n2_s_1_r4, A4);
  Half_Adder half_adder_1 (.A(half_adder_2_c), .B(xnor_1_out), .S(S4));  // open: C
  xnor xnor_2 (xnor_2_out, n2_s_1_r3, A4);
  Half_Adder half_adder_2 (.A(half_adder_3_c), .B(xnor_2_out), .S(S3), .C(half_adder_2_c));
  _2_s u_2_s_1 (.A3(A3), .A2(A2), .A1(A1), .Ao(Ao), .R4(n2_s_1_r4), .R3(n2_s_1_r3), .R2(n2_s_1_r2), .R1(n2_s_1_r1));
  xnor xnor_3 (xnor_3_out, n2_s_1_r2, A4);
  Half_Adder half_adder_3 (.A(half_adder_4_c), .B(xnor_3_out), .S(S2), .C(half_adder_3_c));
  xnor xnor_4 (xnor_4_out, n2_s_1_r1, A4);
  Half_Adder half_adder_4 (.A(not_1_out), .B(xnor_4_out), .S(S1), .C(half_adder_4_c));
endmodule

module Add_sub (
  input  B4,
  input  A4,
  input  B3,
  input  A3,
  input  B2,
  input  A2,
  input  B1,
  input  A1,
  input  B0,
  input  A0,
  input  Mode,
  input  Mode_2,
  output Sign_Flag,
  output overflow,
  output n3,
  output n2,
  output n1,
  output n0
);

  wire and_1_out, and_2_out, and_3_out, check_1_s1, check_1_s2, check_1_s3, check_1_s4, check_3_s1,
       check_3_s2, check_3_s3, check_3_s4, full_adder_1_out_4, full_adder_1_out_5, full_adder_2_out_4,
       full_adder_2_out_5, full_adder_3_out_4, full_adder_3_out_5, full_adder_4_out_4, full_adder_4_out_5,
       full_adder_5_out_4, full_adder_5_out_5, or_1_out, or_3_out, xor_1_out;

  and and_1 (and_1_out, A4, full_adder_1_out_4);
  or or_1 (or_1_out, and_1_out, and_2_out);
  xor xor_1 (xor_1_out, or_3_out, B4);
  and and_2 (and_2_out, full_adder_1_out_4, xor_1_out);
  or or_2 (Sign_Flag, or_1_out, and_3_out);
  and and_3 (and_3_out, A4, xor_1_out);
  Full_Adder full_adder_1 (
    .A(full_adder_2_out_5), .B(A4), .C(xor_1_out), .out_4(full_adder_1_out_4), .out_5(full_adder_1_out_5));
  check check_1 (
    .A4(xor_1_out), .A3(B3), .A2(B2), .A1(B1), .Ao(B0), .S4(check_1_s4), .S3(check_1_s3), .S2(check_1_s2),
    .S1(check_1_s1));
  Full_Adder full_adder_2 (
    .A(full_adder_3_out_5), .B(check_3_s4), .C(check_1_s4), .out_4(full_adder_2_out_4),
    .out_5(full_adder_2_out_5));
  xor xor_2 (overflow, full_adder_2_out_5, full_adder_1_out_5);
  Full_Adder full_adder_3 (
    .A(full_adder_4_out_5), .B(check_3_s3), .C(check_1_s3), .out_4(full_adder_3_out_4),
    .out_5(full_adder_3_out_5));
  check check_2 (
    .A4(Sign_Flag), .A3(full_adder_2_out_4), .A2(full_adder_3_out_4), .A1(full_adder_4_out_4),
    .Ao(full_adder_5_out_4), .S4(n3), .S3(n2), .S2(n1), .S1(n0));
  check check_3 (
    .A4(A4), .A3(A3), .A2(A2), .A1(A1), .Ao(A0), .S4(check_3_s4), .S3(check_3_s3), .S2(check_3_s2),
    .S1(check_3_s1));
  Full_Adder full_adder_4 (
    .A(full_adder_5_out_5), .B(check_3_s2), .C(check_1_s2), .out_4(full_adder_4_out_4),
    .out_5(full_adder_4_out_5));
  Full_Adder full_adder_5 (
    .A(1'b0), .B(check_3_s1), .C(check_1_s1), .out_4(full_adder_5_out_4), .out_5(full_adder_5_out_5));
  or or_3 (or_3_out, Mode, Mode_2);
endmodule
